# Fritzing sketch VictronMQQTBridge (saved by Fritzing 0.9.10b)
perfboards: 1

parts:
  V1 = DC Power [voltage=24V]
  R1 = Resistor [tolerance=±5% resistance=2k power=0.25 package=THT]
  U3_5V = LM2596 step down module
  CNY17-3! = Optocoupler [package=THT]
  BMV-712 = Camdenboss CTB0158-4 [part_number=VE.Direct package=THT]
  J3 = male pin header, 2 pins [form="♂ (male)"]
  J4 = female pin header, 2 pins [form="♀ (female)"]
  J5 = male pin header, 2 pins [form="♂ (male)"]
  MPPT_150/70 = Camdenboss CTB0158-4 [part_number=VE.Direct package=THT]
  J6 = male pin header, 2 pins [form="♂ (male)"]
  J7 = female pin header, 2 pins [form="♀ (female)"]
  J8 = female pin header, 2 pins [form="♀ (female)"]
  R2 = Resistor [tolerance=±5% resistance=2k power=0.25 package=THT]
  CNY17-3!_2 = Optocoupler [package=THT]
  R4 = Resistor [tolerance=±5% resistance=10k power=0.25 package=THT]
  Wemos_D1_mini_ESP32 = MH-ET Live Minikit for ESP32
  R3 = Resistor [tolerance=±5% power=0.25 resistance=10k package=THT]
  C1 = Capacitor Polarized [mn=1000μF package=cpol-radial-100uf-25v]

nets:
  N1: V1.V+, J3.pin1
  N2: V1.V-, J3.pin2
  N3: R1.Pin_0, CNY17-3!.Pin_1
  N4: R1.Pin_1, J7.pin1
  N5: U3_5V.IN+, J4.pin1
  N6: U3_5V.IN-, U3_5V.OUT-, J4.pin2, R4.Pin_1, Wemos_D1_mini_ESP32.GND, R3.Pin_1, C1.-
  N7: U3_5V.OUT+, Wemos_D1_mini_ESP32.VCC, C1.+
  N8: CNY17-3!.Pin_2, J7.pin2
  N9: CNY17-3!.Pin_4, Wemos_D1_mini_ESP32.IO27, R3.Pin_0
  N10: CNY17-3!.Pin_5, CNY17-3!_2.Pin_5, Wemos_D1_mini_ESP32.3.3V
  N11: BMV-712.pin1, J5.pin2
  N12: BMV-712.pin3, J5.pin1
  N13: MPPT_150/70.pin1, J6.pin2
  N14: MPPT_150/70.pin3, J6.pin1
  N15: J8.pin1, R2.Pin_1
  N16: J8.pin2, CNY17-3!_2.Pin_2
  N17: R2.Pin_0, CNY17-3!_2.Pin_1
  N18: CNY17-3!_2.Pin_4, R4.Pin_0, Wemos_D1_mini_ESP32.IO16

custom parts:
  LM2596 step down module: LM2596 DC-DC step down power supply module 3 A.
  MH-ET Live Minikit for ESP32: MH-ET Live Minikit for ESP32 ( http://mh.nodebb.com/topic/8/mh-et-live-minikit-for-esp32/2/) PCB footprint is invalid.
